// Logisim project decoCustom.circ as structural Verilog: 2 circuits, main circuit main
module main (
  input  A,
  input  B,
  input  C,
  input  D,
  input  E,
  input  F,
  input  G,
  input  H
);

  wire button_1_out;

  Button button_1 (.out(button_1_out));
  // AND_Gate and_1 has open pins: in0=button_1_out, in1=B, out=open
  // AND_Gate and_2 has open pins: in0=button_1_out, in1=A, out=open
  // AND_Gate and_3 has open pins: in0=button_1_out, in1=C, out=open
  // AND_Gate and_4 has open pins: in0=button_1_out, in1=D, out=open
  // AND_Gate and_5 has open pins: in0=button_1_out, in1=E, out=open
  Deco_custom deco_custom_1 ();  // open: in_1, in_2, in_3, out_4, out_5, out_6, out_7, out_8, out_9, out_10, out_11
  // AND_Gate and_6 has open pins: in0=button_1_out, in1=F, out=open
  // AND_Gate and_7 has open pins: in0=button_1_out, in1=G, out=open
  // AND_Gate and_8 has open pins: in0=button_1_out, in1=H, out=open
endmodule

module Deco_custom (
  input  in_1,
  input  in_2,
  input  in_3,
  output out_4,
  output out_5,
  output out_6,
  output out_7,
  output out_8,
  output out_9,
  output out_10,
  output out_11
);

  wire not_1_out, not_2_out, not_3_out;

  not not_1 (not_1_out, in_1);
  not not_2 (not_2_out, in_2);
  not not_3 (not_3_out, in_3);
  and and_1 (out_4, not_3_out, not_2_out, not_1_out);
  and and_2 (out_5, not_3_out, not_2_out, in_1);
  and and_3 (out_6, not_3_out, in_2, not_1_out);
  and and_4 (out_7, not_3_out, in_2, in_1);
  and and_5 (out_8, in_3, not_2_out, not_1_out);
  and and_6 (out_9, in_3, not_2_out, in_1);
  and and_7 (out_10, in_3, in_2, not_1_out);
  and and_8 (out_11, in_3, in_2, in_1);
endmodule
