// Logisim project maquinaV2.circ as structural Verilog
module main (
  input  A,
  input  B,
  input  C,
  input  D,
  input  E,
  input  F,
  input  G,
  input  H,
  input  I
);

  wire and_1_out, and_2_out, and_3_out, button_1_out, deco_custom_1_out_4, deco_custom_1_out_5,
       deco_custom_1_out_6, deco_custom_1_out_7, deco_custom_1_out_8, deco_custom_1_out_9,
       deco_custom_1_out_10, deco_custom_1_out_11, undriven, undriven_2, undriven_3, undriven_4, undriven_5;

  Button button_1 (.out(button_1_out));
  and and_1 (and_1_out, button_1_out, B);
  and and_2 (and_2_out, button_1_out, A);
  and and_3 (and_3_out, button_1_out, C);
  Deco_custom deco_custom_1 (
    .in_1(and_3_out), .in_2(and_1_out), .in_3(and_2_out), .out_4(deco_custom_1_out_4),
    .out_5(deco_custom_1_out_5), .out_6(deco_custom_1_out_6), .out_7(deco_custom_1_out_7),
    .out_8(deco_custom_1_out_8), .out_9(deco_custom_1_out_9), .out_10(deco_custom_1_out_10),
    .out_11(deco_custom_1_out_11));
  LED led_1 (.in(undriven_5));
  LED led_2 (.in(undriven_3));
  LED led_3 (.in(undriven_4));
  LED led_4 ();  // open: in
  LED led_5 ();  // open: in
  LED led_6 ();  // open: in
  LED led_7 (.in(undriven));
  LED led_8 (.in(undriven_2));
  _7_Segment_Display u_7_segment_display_1 ();  // open: g, f, a, b, e, d, c, dp

  // Notes on the sheet:
  //   Dec Ops
endmodule

module Deco_custom (
  input  in_1,
  input  in_2,
  input  in_3,
  output out_4,
  output out_5,
  output out_6,
  output out_7,
  output out_8,
  output out_9,
  output out_10,
  output out_11
);

  wire not_1_out, not_2_out, not_3_out;

  not not_1 (not_1_out, in_1);
  not not_2 (not_2_out, in_2);
  not not_3 (not_3_out, in_3);
  and and_1 (out_4, not_3_out, not_2_out, not_1_out);
  and and_2 (out_5, not_3_out, not_2_out, in_1);
  and and_3 (out_6, not_3_out, in_2, not_1_out);
  and and_4 (out_7, not_3_out, in_2, in_1);
  and and_5 (out_8, in_3, not_2_out, not_1_out);
  and and_6 (out_9, in_3, not_2_out, in_1);
  and and_7 (out_10, in_3, in_2, not_1_out);
  and and_8 (out_11, in_3, in_2, in_1);
endmodule

module memoria_custom (
  input  D0,
  input  D1,
  input  D2,
  input  A0,
  input  A1,
  input  A2,
  input  CS,
  input  RD,
  input  OE,
  output Mem_vacia,
  output Flag_palabra_con_0_s,
  output Flag_Mem_Full_1_s,
  output S0,
  output S1,
  output S2
);

  wire and_1_out, and_2_out, and_3_out, and_4_out, and_5_out, and_6_out, and_7_out, and_8_out, and_9_out,
       and_10_out, and_11_out, and_12_out, and_13_out, and_14_out, and_15_out, and_16_out, and_17_out,
       and_18_out, and_19_out, and_20_out, and_21_out, and_22_out, and_23_out, and_24_out, and_25_out,
       and_26_out, and_30_out, and_31_out, and_32_out, and_33_out, and_34_out, and_35_out, and_36_out,
       and_37_out, and_38_out, and_39_out, and_40_out, and_41_out, and_42_out, and_43_out, and_44_out,
       and_45_out, and_46_out, d_ff_1_q, d_ff_2_q, d_ff_3_q, d_ff_4_q, d_ff_5_q, d_ff_6_q, d_ff_7_q,
       d_ff_8_q, d_ff_9_q, d_ff_10_q, d_ff_11_q, d_ff_12_q, d_ff_13_q, d_ff_14_q, d_ff_15_q, d_ff_16_q,
       d_ff_17_q, d_ff_18_q, d_ff_19_q, d_ff_20_q, d_ff_21_q, d_ff_22_q, d_ff_23_q, d_ff_24_q,
       deco_custom_1_out_4, deco_custom_1_out_5, deco_custom_1_out_6, deco_custom_1_out_7,
       deco_custom_1_out_8, deco_custom_1_out_9, deco_custom_1_out_10, deco_custom_1_out_11, not_1_out,
       or_1_out, or_2_out, or_3_out, or_4_out, or_5_out, or_6_out, or_7_out, or_8_out, or_9_out, or_10_out,
       or_11_out, or_12_out;

  Deco_custom deco_custom_1 (
    .in_1(A0), .in_2(A1), .in_3(A2), .out_4(deco_custom_1_out_4), .out_5(deco_custom_1_out_5),
    .out_6(deco_custom_1_out_6), .out_7(deco_custom_1_out_7), .out_8(deco_custom_1_out_8),
    .out_9(deco_custom_1_out_9), .out_10(deco_custom_1_out_10), .out_11(deco_custom_1_out_11));
  and and_1 (and_1_out, deco_custom_1_out_4, and_9_out);
  and and_2 (and_2_out, deco_custom_1_out_5, and_9_out);
  and and_3 (and_3_out, deco_custom_1_out_6, and_9_out);
  and and_4 (and_4_out, deco_custom_1_out_7, and_9_out);
  and and_5 (and_5_out, deco_custom_1_out_8, and_9_out);
  and and_6 (and_6_out, deco_custom_1_out_9, and_9_out);
  and and_7 (and_7_out, deco_custom_1_out_10, and_9_out);
  and and_8 (and_8_out, deco_custom_1_out_11, and_9_out);
  and and_9 (and_9_out, CS, not_1_out);
  D_Flip_Flop d_ff_1 (.clk(and_1_out), .D(D0), .Q(d_ff_1_q));  // open: Qn, preset, en, reset
  and and_10 (and_10_out, deco_custom_1_out_4, d_ff_1_q);
  D_Flip_Flop d_ff_2 (.clk(and_2_out), .D(D0), .Q(d_ff_2_q));  // open: Qn, preset, en, reset
  and and_11 (and_11_out, deco_custom_1_out_5, d_ff_2_q);
  D_Flip_Flop d_ff_3 (.clk(and_3_out), .D(D0), .Q(d_ff_3_q));  // open: Qn, preset, en, reset
  and and_12 (and_12_out, deco_custom_1_out_6, d_ff_3_q);
  D_Flip_Flop d_ff_4 (.clk(and_4_out), .D(D0), .Q(d_ff_4_q));  // open: Qn, preset, en, reset
  and and_13 (and_13_out, deco_custom_1_out_7, d_ff_4_q);
  D_Flip_Flop d_ff_5 (.clk(and_5_out), .D(D0), .Q(d_ff_5_q));  // open: Qn, preset, en, reset
  and and_14 (and_14_out, deco_custom_1_out_8, d_ff_5_q);
  D_Flip_Flop d_ff_6 (.clk(and_6_out), .D(D0), .Q(d_ff_6_q));  // open: Qn, preset, en, reset
  and and_15 (and_15_out, deco_custom_1_out_9, d_ff_6_q);
  D_Flip_Flop d_ff_7 (.clk(and_7_out), .D(D0), .Q(d_ff_7_q));  // open: Qn, preset, en, reset
  and and_16 (and_16_out, deco_custom_1_out_10, d_ff_7_q);
  D_Flip_Flop d_ff_8 (.clk(and_8_out), .D(D0), .Q(d_ff_8_q));  // open: Qn, preset, en, reset
  and and_17 (and_17_out, deco_custom_1_out_11, d_ff_8_q);
  not not_1 (not_1_out, RD);
  or or_1 (or_1_out, and_17_out, and_16_out, and_15_out, and_14_out, and_13_out, and_12_out, and_11_out, and_10_out);
  and and_18 (and_18_out, CS, RD, OE);
  D_Flip_Flop d_ff_9 (.clk(and_1_out), .D(D1), .Q(d_ff_9_q));  // open: Qn, preset, en, reset
  and and_19 (and_19_out, deco_custom_1_out_4, d_ff_9_q);
  D_Flip_Flop d_ff_10 (.clk(and_2_out), .D(D1), .Q(d_ff_10_q));  // open: Qn, preset, en, reset
  and and_20 (and_20_out, deco_custom_1_out_5, d_ff_10_q);
  D_Flip_Flop d_ff_11 (.clk(and_3_out), .D(D1), .Q(d_ff_11_q));  // open: Qn, preset, en, reset
  and and_21 (and_21_out, deco_custom_1_out_6, d_ff_11_q);
  D_Flip_Flop d_ff_12 (.clk(and_4_out), .D(D1), .Q(d_ff_12_q));  // open: Qn, preset, en, reset
  and and_22 (and_22_out, deco_custom_1_out_7, d_ff_12_q);
  D_Flip_Flop d_ff_13 (.clk(and_5_out), .D(D1), .Q(d_ff_13_q));  // open: Qn, preset, en, reset
  and and_23 (and_23_out, deco_custom_1_out_8, d_ff_13_q);
  D_Flip_Flop d_ff_14 (.clk(and_6_out), .D(D1), .Q(d_ff_14_q));  // open: Qn, preset, en, reset
  and and_24 (and_24_out, deco_custom_1_out_9, d_ff_14_q);
  D_Flip_Flop d_ff_15 (.clk(and_7_out), .D(D1), .Q(d_ff_15_q));  // open: Qn, preset, en, reset
  and and_25 (and_25_out, deco_custom_1_out_10, d_ff_15_q);
  D_Flip_Flop d_ff_16 (.clk(and_8_out), .D(D1), .Q(d_ff_16_q));  // open: Qn, preset, en, reset
  and and_26 (and_26_out, deco_custom_1_out_11, d_ff_16_q);
  or or_2 (or_2_out, and_26_out, and_25_out, and_24_out, and_23_out, and_22_out, and_21_out, and_20_out, and_19_out);
  and and_27 (S0, or_1_out, and_18_out);
  and and_28 (S1, and_18_out, or_2_out);
  and and_29 (S2, and_18_out, or_3_out);
  D_Flip_Flop d_ff_17 (.clk(and_1_out), .D(D2), .Q(d_ff_17_q));  // open: Qn, preset, en, reset
  D_Flip_Flop d_ff_18 (.clk(and_2_out), .D(D2), .Q(d_ff_18_q));  // open: Qn, preset, en, reset
  D_Flip_Flop d_ff_19 (.clk(and_3_out), .D(D2), .Q(d_ff_19_q));  // open: Qn, preset, en, reset
  D_Flip_Flop d_ff_20 (.clk(and_4_out), .D(D2), .Q(d_ff_20_q));  // open: Qn, preset, en, reset
  D_Flip_Flop d_ff_21 (.clk(and_5_out), .D(D2), .Q(d_ff_21_q));  // open: Qn, preset, en, reset
  D_Flip_Flop d_ff_22 (.clk(and_6_out), .D(D2), .Q(d_ff_22_q));  // open: Qn, preset, en, reset
  D_Flip_Flop d_ff_23 (.clk(and_7_out), .D(D2), .Q(d_ff_23_q));  // open: Qn, preset, en, reset
  D_Flip_Flop d_ff_24 (.clk(and_8_out), .D(D2), .Q(d_ff_24_q));  // open: Qn, preset, en, reset
  and and_30 (and_30_out, deco_custom_1_out_4, d_ff_17_q);
  and and_31 (and_31_out, deco_custom_1_out_5, d_ff_18_q);
  and and_32 (and_32_out, deco_custom_1_out_6, d_ff_19_q);
  and and_33 (and_33_out, deco_custom_1_out_7, d_ff_20_q);
  and and_34 (and_34_out, deco_custom_1_out_8, d_ff_21_q);
  and and_35 (and_35_out, deco_custom_1_out_9, d_ff_22_q);
  and and_36 (and_36_out, deco_custom_1_out_10, d_ff_23_q);
  and and_37 (and_37_out, deco_custom_1_out_11, d_ff_24_q);
  or or_3 (or_3_out, and_37_out, and_36_out, and_35_out, and_34_out, and_33_out, and_32_out, and_31_out, and_30_out);
  and and_38 (and_38_out, d_ff_17_q, d_ff_9_q, d_ff_1_q);
  or or_4 (or_4_out, d_ff_1_q, d_ff_9_q, d_ff_17_q);
  or or_5 (or_5_out, d_ff_2_q, d_ff_10_q, d_ff_18_q);
  and and_39 (and_39_out, d_ff_18_q, d_ff_10_q, d_ff_2_q);
  or or_6 (or_6_out, d_ff_3_q, d_ff_11_q, d_ff_19_q);
  and and_40 (and_40_out, d_ff_19_q, d_ff_11_q, d_ff_3_q);
  or or_7 (or_7_out, d_ff_4_q, d_ff_12_q, d_ff_20_q);
  and and_41 (and_41_out, d_ff_20_q, d_ff_12_q, d_ff_4_q);
  or or_8 (or_8_out, d_ff_5_q, d_ff_13_q, d_ff_21_q);
  and and_42 (and_42_out, d_ff_21_q, d_ff_13_q, d_ff_5_q);
  or or_9 (or_9_out, d_ff_6_q, d_ff_14_q, d_ff_22_q);
  and and_43 (and_43_out, d_ff_22_q, d_ff_14_q, d_ff_6_q);
  or or_10 (or_10_out, d_ff_7_q, d_ff_15_q, d_ff_23_q);
  and and_44 (and_44_out, d_ff_23_q, d_ff_15_q, d_ff_7_q);
  or or_11 (or_11_out, d_ff_8_q, d_ff_16_q, d_ff_24_q);
  and and_45 (and_45_out, d_ff_24_q, d_ff_16_q, d_ff_8_q);
  or or_12 (or_12_out, or_11_out, or_10_out, or_9_out, or_8_out, or_7_out, or_6_out, or_5_out, or_4_out);
  not not_2 (Mem_vacia, or_12_out);
  and and_46 (and_46_out, or_4_out, or_5_out, or_6_out, or_7_out, or_8_out, or_9_out, or_10_out, or_11_out);
  and and_47 (Flag_Mem_Full_1_s, and_38_out, and_39_out, and_40_out, and_41_out, and_42_out, and_43_out, and_44_out, and_45_out);
  not not_3 (Flag_palabra_con_0_s, and_46_out);
endmodule

module Mem_Controller (
  input  D,
  input  E,
  input  F,
  input  G,
  input  H,
  input  I,
  input  Mem_vacia_flag,
  input  Btn,
  input  Guarda,
  input  Muestra,
  input  Borra_todo,
  output D_2,
  output E_2,
  output F_2,
  output G_2,
  output H_2,
  output I_2,
  output CS_OUT,
  output RD_OUT,
  output OE_OUT
);

  wire and_1_out, and_2_out, and_3_out, and_5_out, and_6_out, j_k_ff_1_q, j_k_ff_2_q, j_k_ff_3_q, not_1_out,
       undriven;

  and and_1 (and_1_out, Btn, Guarda);
  and and_2 (and_2_out, Muestra, Btn);
  or or_1 (CS_OUT, and_1_out, and_2_out, and_3_out);
  not not_1 (not_1_out, Guarda);
  and and_3 (and_3_out, Borra_todo, Btn);
  and and_4 (RD_OUT, not_1_out, Muestra);
  J_K_Flip_Flop j_k_ff_1 (.J(undriven), .clk(undriven), .K(undriven), .Q(j_k_ff_1_q));  // open: Qn, preset, en, reset
  buf and_5 (and_5_out, j_k_ff_1_q);  // AND_Gate
  J_K_Flip_Flop j_k_ff_2 (.J(and_5_out), .clk(undriven), .K(and_5_out), .Q(j_k_ff_2_q));  // open: Qn, preset, en, reset
  and and_6 (and_6_out, j_k_ff_2_q, and_5_out);
  J_K_Flip_Flop j_k_ff_3 (.J(and_6_out), .clk(undriven), .K(and_6_out), .Q(j_k_ff_3_q));  // open: Qn, preset, en, reset
  // AND_Gate and_7 has open pins: in1=j_k_ff_3_q, in3=and_6_out, out=open

  assign OE_OUT = Muestra;

  // Notes on the sheet:
  //   c
  //   b
  //   a
endmodule
