// Logisim project maquinaV2_3_1.circ as structural Verilog: 12 circuits, main circuit main
module main (
  input  A,
  input  B,
  input  C,
  input  D,
  input  E,
  input  F,
  input  G,
  input  H,
  input  I
);

  wire and_1_out, and_2_out, and_3_out, and_4_out, and_5_out, and_6_out, and_7_out, and_8_out, and_9_out,
       and_10_out, and_11_out, and_12_out, button_1_out, decodificador_de_3_bits_1_out_4,
       decodificador_de_3_bits_1_out_5, decodificador_de_3_bits_1_out_6, decodificador_de_3_bits_1_out_7,
       decodificador_de_3_bits_1_out_8, decodificador_de_3_bits_1_out_9, decodificador_de_3_bits_1_out_10,
       decodificador_de_3_bits_1_out_11, display_controller_1_a, display_controller_1_b,
       display_controller_1_c, display_controller_1_d, display_controller_1_e, display_controller_1_f,
       display_controller_1_g, Mem_8x3_flag_mem_full_1_s, Mem_8x3_flag_palabra_con_0_s, Mem_8x3_mem_vacia,
       Mem_8x3_s0, Mem_8x3_s1, Mem_8x3_s2, Mem_Controller_cs_out, Mem_Controller_d_2, Mem_Controller_del,
       Mem_Controller_e_2, Mem_Controller_f_2, Mem_Controller_g_2, Mem_Controller_h_2, Mem_Controller_i_2,
       Mem_Controller_oe_out, Mem_Controller_rd_out, or_1_out, or_2_out, or_3_out;

  Button button_1 (.out(button_1_out));
  and and_1 (and_1_out, button_1_out, A);
  and and_2 (and_2_out, button_1_out, B);
  and and_3 (and_3_out, button_1_out, D);
  and and_4 (and_4_out, button_1_out, C);
  Decodificador_de_3_bits decodificador_de_3_bits_1 (
    .in_1(and_4_out), .in_2(and_2_out), .in_3(and_1_out), .out_4(decodificador_de_3_bits_1_out_4),
    .out_5(decodificador_de_3_bits_1_out_5), .out_6(decodificador_de_3_bits_1_out_6),
    .out_7(decodificador_de_3_bits_1_out_7), .out_8(decodificador_de_3_bits_1_out_8),
    .out_9(decodificador_de_3_bits_1_out_9), .out_10(decodificador_de_3_bits_1_out_10),
    .out_11(decodificador_de_3_bits_1_out_11));
  and and_5 (and_5_out, button_1_out, E);
  and and_6 (and_6_out, button_1_out, F);
  and and_7 (and_7_out, button_1_out, decodificador_de_3_bits_1_out_4);
  and and_8 (and_8_out, button_1_out, decodificador_de_3_bits_1_out_5);
  and and_9 (and_9_out, button_1_out, decodificador_de_3_bits_1_out_8);
  and and_10 (and_10_out, button_1_out, G);
  and and_11 (and_11_out, button_1_out, H);
  and and_12 (and_12_out, button_1_out, I);
  Mem_controller Mem_Controller (
    ._000(and_7_out), ._001(and_8_out), ._100(and_9_out), .D(and_3_out), .E(and_5_out), .F(and_6_out),
    .G(and_10_out), .H(and_11_out), .I(and_12_out), .CS_OUT(Mem_Controller_cs_out),
    .RD_OUT(Mem_Controller_rd_out), .OE_OUT(Mem_Controller_oe_out), .DEL(Mem_Controller_del),
    .D_2(Mem_Controller_d_2), .E_2(Mem_Controller_e_2), .F_2(Mem_Controller_f_2), .G_2(Mem_Controller_g_2),
    .H_2(Mem_Controller_h_2), .I_2(Mem_Controller_i_2));
  ALU ALU ();  // open: D, E, F, G, H, I, _010, _011, _101, _110, _111, SD0, SD1, SD2, SL0, SL1, SL2, Zero_flag, Carry_Flag, Overflow
  Memoria_8_x_3 Mem_8x3 (
    .A0(Mem_Controller_d_2), .A1(Mem_Controller_e_2), .A2(Mem_Controller_f_2), .DEL(Mem_Controller_del),
    .D0(Mem_Controller_g_2), .D1(Mem_Controller_h_2), .D2(Mem_Controller_i_2), .CS(Mem_Controller_cs_out),
    .RD(Mem_Controller_rd_out), .OE(Mem_Controller_oe_out), .S0(Mem_8x3_s0), .S1(Mem_8x3_s1),
    .S2(Mem_8x3_s2), .Mem_vacia(Mem_8x3_mem_vacia), .Flag_palabra_con_0_s(Mem_8x3_flag_palabra_con_0_s),
    .Flag_Mem_Full_1_s(Mem_8x3_flag_mem_full_1_s));
  LED SL2 ();  // open: in
  LED SL1 ();  // open: in
  LED SL0 ();  // open: in
  // OR_Gate or_1 has open pins: out=or_1_out
  // OR_Gate or_2 has open pins: out=or_2_out
  // OR_Gate or_3 has open pins: out=or_3_out
  _7_Segment_Display u_7_segment_display_1 (
    .g(display_controller_1_g), .f(display_controller_1_f), .a(display_controller_1_a),
    .b(display_controller_1_b), .e(display_controller_1_e), .d(display_controller_1_d),
    .c(display_controller_1_c));  // open: dp
  Display_controller display_controller_1 (
    .e0(or_3_out), .e1(or_2_out), .e2(or_1_out), .A(display_controller_1_a), .B(display_controller_1_b),
    .C(display_controller_1_c), .D(display_controller_1_d), .E(display_controller_1_e),
    .F(display_controller_1_f), .G(display_controller_1_g));
  LED Carry ();  // open: in
  LED Overflow ();  // open: in
  LED Zero ();  // open: in
  LED Palabra_con_0 (.in(Mem_8x3_flag_palabra_con_0_s));
  LED Mem_full (.in(Mem_8x3_flag_mem_full_1_s));
  LED \Mem_Vacía__prueba  (.in(Mem_8x3_mem_vacia));

  // Notes on the sheet:
  //   Dec Ops
  //   Salida leds
  //   Salida digital
  //   Flags
endmodule

module Decodificador_de_3_bits (
  input  in_1,
  input  in_2,
  input  in_3,
  output out_4,
  output out_5,
  output out_6,
  output out_7,
  output out_8,
  output out_9,
  output out_10,
  output out_11
);

  wire not_1_out, not_2_out, not_3_out;

  not not_1 (not_1_out, in_1);
  not not_2 (not_2_out, in_2);
  not not_3 (not_3_out, in_3);
  and and_1 (out_4, not_3_out, not_2_out, not_1_out);
  and and_2 (out_5, not_3_out, not_2_out, in_1);
  and and_3 (out_6, not_3_out, in_2, not_1_out);
  and and_4 (out_7, not_3_out, in_2, in_1);
  and and_5 (out_8, in_3, not_2_out, not_1_out);
  and and_6 (out_9, in_3, not_2_out, in_1);
  and and_7 (out_10, in_3, in_2, not_1_out);
  and and_8 (out_11, in_3, in_2, in_1);
endmodule

module Memoria_8_x_3 (
  input  DEL,
  input  D0,
  input  D1,
  input  D2,
  input  A0,
  input  A1,
  input  A2,
  input  CS,
  input  RD,
  input  OE,
  output Mem_vacia,
  output Flag_palabra_con_0_s,
  output Flag_Mem_Full_1_s,
  output S0,
  output S1,
  output S2
);

  wire and_1_out, and_2_out, and_3_out, and_4_out, and_5_out, and_6_out, and_7_out, and_8_out, and_9_out,
       and_10_out, and_11_out, and_12_out, and_13_out, and_14_out, and_15_out, and_16_out, and_17_out,
       and_18_out, and_19_out, and_20_out, and_21_out, and_22_out, and_23_out, and_24_out, and_25_out,
       and_26_out, and_30_out, and_31_out, and_32_out, and_33_out, and_34_out, and_35_out, and_36_out,
       and_37_out, and_38_out, and_39_out, and_40_out, and_41_out, and_42_out, and_43_out, and_44_out,
       and_45_out, and_46_out, d_ff_1_q, d_ff_2_q, d_ff_3_q, d_ff_4_q, d_ff_5_q, d_ff_6_q, d_ff_7_q,
       d_ff_8_q, d_ff_9_q, d_ff_10_q, d_ff_11_q, d_ff_12_q, d_ff_13_q, d_ff_14_q, d_ff_15_q, d_ff_16_q,
       d_ff_17_q, d_ff_18_q, d_ff_19_q, d_ff_20_q, d_ff_21_q, d_ff_22_q, d_ff_23_q, d_ff_24_q,
       decodificador_de_3_bits_1_out_4, decodificador_de_3_bits_1_out_5, decodificador_de_3_bits_1_out_6,
       decodificador_de_3_bits_1_out_7, decodificador_de_3_bits_1_out_8, decodificador_de_3_bits_1_out_9,
       decodificador_de_3_bits_1_out_10, decodificador_de_3_bits_1_out_11, not_1_out, or_1_out, or_2_out,
       or_3_out, or_4_out, or_5_out, or_6_out, or_7_out, or_8_out, or_9_out, or_10_out, or_11_out, or_12_out,
       or_13_out, or_14_out, or_15_out, or_16_out, or_17_out, or_18_out, or_19_out;

  Decodificador_de_3_bits decodificador_de_3_bits_1 (
    .in_1(A0), .in_2(A1), .in_3(A2), .out_4(decodificador_de_3_bits_1_out_4),
    .out_5(decodificador_de_3_bits_1_out_5), .out_6(decodificador_de_3_bits_1_out_6),
    .out_7(decodificador_de_3_bits_1_out_7), .out_8(decodificador_de_3_bits_1_out_8),
    .out_9(decodificador_de_3_bits_1_out_9), .out_10(decodificador_de_3_bits_1_out_10),
    .out_11(decodificador_de_3_bits_1_out_11));
  and and_1 (and_1_out, decodificador_de_3_bits_1_out_4, and_9_out);
  and and_2 (and_2_out, decodificador_de_3_bits_1_out_5, and_9_out);
  and and_3 (and_3_out, decodificador_de_3_bits_1_out_6, and_9_out);
  and and_4 (and_4_out, decodificador_de_3_bits_1_out_7, and_9_out);
  and and_5 (and_5_out, decodificador_de_3_bits_1_out_8, and_9_out);
  and and_6 (and_6_out, decodificador_de_3_bits_1_out_9, and_9_out);
  and and_7 (and_7_out, decodificador_de_3_bits_1_out_10, and_9_out);
  and and_8 (and_8_out, decodificador_de_3_bits_1_out_11, and_9_out);
  or or_1 (or_1_out, and_2_out, DEL);
  or or_2 (or_2_out, and_3_out, DEL);
  or or_3 (or_3_out, and_4_out, DEL);
  or or_4 (or_4_out, and_5_out, DEL);
  or or_5 (or_5_out, and_6_out, DEL);
  or or_6 (or_6_out, and_7_out, DEL);
  or or_7 (or_7_out, and_8_out, DEL);
  and and_9 (and_9_out, CS, not_1_out);
  D_Flip_Flop d_ff_1 (.clk(and_1_out), .D(D0), .Q(d_ff_1_q), .reset(DEL));  // open: Qn, preset, en
  and and_10 (and_10_out, decodificador_de_3_bits_1_out_4, d_ff_1_q);
  D_Flip_Flop d_ff_2 (.clk(or_1_out), .D(D0), .Q(d_ff_2_q));  // open: Qn, preset, en, reset
  and and_11 (and_11_out, decodificador_de_3_bits_1_out_5, d_ff_2_q);
  D_Flip_Flop d_ff_3 (.clk(or_2_out), .D(D0), .Q(d_ff_3_q));  // open: Qn, preset, en, reset
  and and_12 (and_12_out, decodificador_de_3_bits_1_out_6, d_ff_3_q);
  D_Flip_Flop d_ff_4 (.clk(or_3_out), .D(D0), .Q(d_ff_4_q));  // open: Qn, preset, en, reset
  and and_13 (and_13_out, decodificador_de_3_bits_1_out_7, d_ff_4_q);
  D_Flip_Flop d_ff_5 (.clk(or_4_out), .D(D0), .Q(d_ff_5_q));  // open: Qn, preset, en, reset
  and and_14 (and_14_out, decodificador_de_3_bits_1_out_8, d_ff_5_q);
  D_Flip_Flop d_ff_6 (.clk(or_5_out), .D(D0), .Q(d_ff_6_q));  // open: Qn, preset, en, reset
  and and_15 (and_15_out, decodificador_de_3_bits_1_out_9, d_ff_6_q);
  D_Flip_Flop d_ff_7 (.clk(or_6_out), .D(D0), .Q(d_ff_7_q));  // open: Qn, preset, en, reset
  and and_16 (and_16_out, decodificador_de_3_bits_1_out_10, d_ff_7_q);
  D_Flip_Flop d_ff_8 (.clk(or_7_out), .D(D0), .Q(d_ff_8_q));  // open: Qn, preset, en, reset
  and and_17 (and_17_out, decodificador_de_3_bits_1_out_11, d_ff_8_q);
  not not_1 (not_1_out, RD);
  or or_8 (or_8_out, and_17_out, and_16_out, and_15_out, and_14_out, and_13_out, and_12_out, and_11_out, and_10_out);
  and and_18 (and_18_out, CS, RD, OE);
  D_Flip_Flop d_ff_9 (.clk(and_1_out), .D(D1), .Q(d_ff_9_q));  // open: Qn, preset, en, reset
  and and_19 (and_19_out, decodificador_de_3_bits_1_out_4, d_ff_9_q);
  D_Flip_Flop d_ff_10 (.clk(or_1_out), .D(D1), .Q(d_ff_10_q));  // open: Qn, preset, en, reset
  and and_20 (and_20_out, decodificador_de_3_bits_1_out_5, d_ff_10_q);
  D_Flip_Flop d_ff_11 (.clk(or_2_out), .D(D1), .Q(d_ff_11_q));  // open: Qn, preset, en, reset
  and and_21 (and_21_out, decodificador_de_3_bits_1_out_6, d_ff_11_q);
  D_Flip_Flop d_ff_12 (.clk(or_3_out), .D(D1), .Q(d_ff_12_q));  // open: Qn, preset, en, reset
  and and_22 (and_22_out, decodificador_de_3_bits_1_out_7, d_ff_12_q);
  D_Flip_Flop d_ff_13 (.clk(or_4_out), .D(D1), .Q(d_ff_13_q));  // open: Qn, preset, en, reset
  and and_23 (and_23_out, decodificador_de_3_bits_1_out_8, d_ff_13_q);
  D_Flip_Flop d_ff_14 (.clk(or_5_out), .D(D1), .Q(d_ff_14_q));  // open: Qn, preset, en, reset
  and and_24 (and_24_out, decodificador_de_3_bits_1_out_9, d_ff_14_q);
  D_Flip_Flop d_ff_15 (.clk(or_6_out), .D(D1), .Q(d_ff_15_q));  // open: Qn, preset, en, reset
  and and_25 (and_25_out, decodificador_de_3_bits_1_out_10, d_ff_15_q);
  D_Flip_Flop d_ff_16 (.clk(or_7_out), .D(D1), .Q(d_ff_16_q));  // open: Qn, preset, en, reset
  and and_26 (and_26_out, decodificador_de_3_bits_1_out_11, d_ff_16_q);
  or or_9 (or_9_out, and_26_out, and_25_out, and_24_out, and_23_out, and_22_out, and_21_out, and_20_out, and_19_out);
  and and_27 (S0, or_8_out, and_18_out);
  and and_28 (S1, and_18_out, or_9_out);
  and and_29 (S2, and_18_out, or_10_out);
  D_Flip_Flop d_ff_17 (.clk(and_1_out), .D(D2), .Q(d_ff_17_q));  // open: Qn, preset, en, reset
  D_Flip_Flop d_ff_18 (.clk(or_1_out), .D(D2), .Q(d_ff_18_q));  // open: Qn, preset, en, reset
  D_Flip_Flop d_ff_19 (.clk(or_2_out), .D(D2), .Q(d_ff_19_q));  // open: Qn, preset, en, reset
  D_Flip_Flop d_ff_20 (.clk(or_3_out), .D(D2), .Q(d_ff_20_q));  // open: Qn, preset, en, reset
  D_Flip_Flop d_ff_21 (.clk(or_4_out), .D(D2), .Q(d_ff_21_q));  // open: Qn, preset, en, reset
  D_Flip_Flop d_ff_22 (.clk(or_5_out), .D(D2), .Q(d_ff_22_q));  // open: Qn, preset, en, reset
  D_Flip_Flop d_ff_23 (.clk(or_6_out), .D(D2), .Q(d_ff_23_q));  // open: Qn, preset, en, reset
  D_Flip_Flop d_ff_24 (.clk(or_7_out), .D(D2), .Q(d_ff_24_q));  // open: Qn, preset, en, reset
  and and_30 (and_30_out, decodificador_de_3_bits_1_out_4, d_ff_17_q);
  and and_31 (and_31_out, decodificador_de_3_bits_1_out_5, d_ff_18_q);
  and and_32 (and_32_out, decodificador_de_3_bits_1_out_6, d_ff_19_q);
  and and_33 (and_33_out, decodificador_de_3_bits_1_out_7, d_ff_20_q);
  and and_34 (and_34_out, decodificador_de_3_bits_1_out_8, d_ff_21_q);
  and and_35 (and_35_out, decodificador_de_3_bits_1_out_9, d_ff_22_q);
  and and_36 (and_36_out, decodificador_de_3_bits_1_out_10, d_ff_23_q);
  and and_37 (and_37_out, decodificador_de_3_bits_1_out_11, d_ff_24_q);
  or or_10 (or_10_out, and_37_out, and_36_out, and_35_out, and_34_out, and_33_out, and_32_out, and_31_out, and_30_out);
  and and_38 (and_38_out, d_ff_17_q, d_ff_9_q, d_ff_1_q);
  or or_11 (or_11_out, d_ff_1_q, d_ff_9_q, d_ff_17_q);
  or or_12 (or_12_out, d_ff_2_q, d_ff_10_q, d_ff_18_q);
  and and_39 (and_39_out, d_ff_18_q, d_ff_10_q, d_ff_2_q);
  or or_13 (or_13_out, d_ff_3_q, d_ff_11_q, d_ff_19_q);
  and and_40 (and_40_out, d_ff_19_q, d_ff_11_q, d_ff_3_q);
  or or_14 (or_14_out, d_ff_4_q, d_ff_12_q, d_ff_20_q);
  and and_41 (and_41_out, d_ff_20_q, d_ff_12_q, d_ff_4_q);
  or or_15 (or_15_out, d_ff_5_q, d_ff_13_q, d_ff_21_q);
  and and_42 (and_42_out, d_ff_21_q, d_ff_13_q, d_ff_5_q);
  or or_16 (or_16_out, d_ff_6_q, d_ff_14_q, d_ff_22_q);
  and and_43 (and_43_out, d_ff_22_q, d_ff_14_q, d_ff_6_q);
  or or_17 (or_17_out, d_ff_7_q, d_ff_15_q, d_ff_23_q);
  and and_44 (and_44_out, d_ff_23_q, d_ff_15_q, d_ff_7_q);
  or or_18 (or_18_out, d_ff_8_q, d_ff_16_q, d_ff_24_q);
  and and_45 (and_45_out, d_ff_24_q, d_ff_16_q, d_ff_8_q);
  or or_19 (or_19_out, or_18_out, or_17_out, or_16_out, or_15_out, or_14_out, or_13_out, or_12_out, or_11_out);
  not not_2 (Mem_vacia, or_19_out);
  and and_46 (and_46_out, or_11_out, or_12_out, or_13_out, or_14_out, or_15_out, or_16_out, or_17_out, or_18_out);
  and and_47 (Flag_Mem_Full_1_s, and_38_out, and_39_out, and_40_out, and_41_out, and_42_out, and_43_out, and_44_out, and_45_out);
  not not_3 (Flag_palabra_con_0_s, and_46_out);
endmodule

module ALU (
  input  D,
  input  E,
  input  F,
  input  G,
  input  H,
  input  I,
  input  _010,
  input  _011,
  input  _101,
  input  _110,
  input  _111,
  output SL0,
  output SL1,
  output SL2,
  output Zero_flag,
  output Carry_Flag,
  output Overflow,
  output SD0,
  output SD1,
  output SD2
);

  wire Funcion_s, Inversor_C2_s0, Inversor_C2_s1, Inversor_C2_s2, Paridad_out_8, resta_1_overflow,
       resta_1_s0, resta_1_s1, Sum_completo_carry_flag, Sum_completo_overflow, Sum_completo_s0,
       Sum_completo_s1, Sum_completo_s2;

  Funcion Funcion (.CS(_011), .D(D), .E(E), .F(F), .G(G), .S(Funcion_s));
  Paridad Paridad (.D(D), .E(E), .F(F), .G(G), .H(H), .I(I), .CS(_101), .out_8(Paridad_out_8));
  Inversor_C2 Inversor_C2 (
    .D(D), .E(E), .F(F), .CS(_110), .S0(Inversor_C2_s0), .S1(Inversor_C2_s1), .S2(Inversor_C2_s2));  // open: Zero_F
  Resta resta_1 (
    .D(D), .E(E), .F(F), .G(G), .CS(_111), .S0(resta_1_s0), .S1(resta_1_s1), .Overflow(resta_1_overflow));  // open: ZeroF
  or or_1 (SD0, Sum_completo_s0, Funcion_s);
  or or_2 (SD1, Sum_completo_s1, resta_1_s0);
  or or_3 (SD2, Sum_completo_s2, resta_1_s1);
  Sumador_ALU Sum_completo (
    .D(D), .E(E), .F(F), .G(G), .H(H), .I(I), .CS(_010), .S2(Sum_completo_s2), .S1(Sum_completo_s1),
    .S0(Sum_completo_s0), .OVERFLOW(Sum_completo_overflow), .Carry_Flag(Sum_completo_carry_flag));
  or or_4 (SL0, Funcion_s, Inversor_C2_s0, Sum_completo_s0, Paridad_out_8);
  or or_5 (SL1, Inversor_C2_s1, Sum_completo_s1);
  or or_6 (SL2, Sum_completo_s2, Inversor_C2_s2);
  nor nor_1 (Zero_flag, resta_1_s1, Funcion_s, Inversor_C2_s2, Sum_completo_s2, Paridad_out_8, Inversor_C2_s1, Inversor_C2_s0, Sum_completo_s1, Sum_completo_s0, resta_1_s0);
  buf or_7 (Carry_Flag, Sum_completo_overflow);  // OR_Gate
  or or_8 (Overflow, Sum_completo_carry_flag, resta_1_overflow);
endmodule

module Mem_controller (
  input  D,
  input  E,
  input  F,
  input  G,
  input  H,
  input  I,
  input  _000,
  input  _001,
  input  _100,
  output D_2,
  output E_2,
  output F_2,
  output G_2,
  output H_2,
  output CS_OUT,
  output RD_OUT,
  output OE_OUT,
  output DEL,
  output I_2
);

  wire and_1_out, and_2_out, and_3_out, not_1_out, not_2_out, not_3_out, not_4_out;

  buf and_1 (and_1_out, _000);  // AND_Gate
  buf and_2 (and_2_out, _001);  // AND_Gate
  or or_1 (CS_OUT, and_1_out, and_2_out, and_3_out);
  not not_1 (not_1_out, _000);
  buf and_3 (and_3_out, _100);  // AND_Gate
  and and_4 (RD_OUT, not_1_out, _001);
  not not_2 (not_2_out, _100);
  not not_3 (not_3_out, _100);
  not not_4 (not_4_out, _100);
  and and_5 (G_2, G, not_2_out);
  and and_6 (H_2, H, not_3_out);
  and and_7 (I_2, I, not_4_out);

  assign D_2 = D;
  assign DEL = _100;
  assign E_2 = E;
  assign F_2 = F;
  assign OE_OUT = _001;

  // Notes on the sheet:
  //   G_2: pull=down
  //   H_2: pull=down
  //   I_2: pull=down
endmodule

module Display_controller (
  input  e0,
  input  e1,
  input  e2,
  output A,
  output B,
  output C,
  output D,
  output E,
  output F,
  output G
);

  wire not_1_out, not_2_out, not_3_out, or_1_out, or_2_out, or_3_out, or_4_out, or_6_out, or_7_out, or_8_out,
       or_9_out, or_10_out, or_11_out, or_12_out, or_13_out, or_14_out;

  not not_1 (not_1_out, e0);
  not not_2 (not_2_out, e1);
  not not_3 (not_3_out, e2);
  or or_1 (or_1_out, not_3_out, e1, e0);
  or or_2 (or_2_out, not_1_out, e1, e2);
  or or_3 (or_3_out, not_1_out, not_2_out, e2);
  or or_4 (or_4_out, not_1_out, e1, not_3_out);
  or or_5 (C, e0, not_2_out, e2);
  or or_6 (or_6_out, e0, e1, not_3_out);
  or or_7 (or_7_out, not_3_out, not_2_out, not_1_out);
  or or_8 (or_8_out, not_1_out, e2, e1);
  or or_9 (or_9_out, not_1_out, e1);
  or or_10 (or_10_out, e0, not_3_out);
  or or_11 (or_11_out, not_2_out, not_3_out);
  or or_12 (or_12_out, e0, not_2_out);
  or or_13 (or_13_out, e0, e1);
  or or_14 (or_14_out, not_1_out, not_2_out, not_3_out);
  and and_1 (A, or_1_out, or_2_out);
  and and_2 (B, or_3_out, or_4_out);
  and and_3 (D, or_6_out, or_7_out, or_8_out);
  and and_4 (E, not_3_out, or_9_out);
  and and_5 (F, or_10_out, or_11_out, or_12_out);
  and and_6 (G, or_13_out, or_14_out);

  // Notes on the sheet:
  //   C
  //   D
  //   A
  //   B
  //   E
  //   F
endmodule

module Sumador_Completo_2_bits (
  input  e0,
  input  e1,
  input  Cin,
  output S,
  output Cout
);

  wire and_1_out, and_2_out, xor_1_out;

  and and_1 (and_1_out, xor_1_out, Cin);
  and and_2 (and_2_out, e1, e0);
  xor xor_1 (xor_1_out, e0, e1);
  or or_1 (Cout, and_1_out, and_2_out);
  xor xor_2 (S, xor_1_out, Cin);
endmodule

module Sumador_ALU (
  input  D,
  input  E,
  input  F,
  input  G,
  input  H,
  input  I,
  input  CS,
  output S2,
  output S1,
  output S0,
  output OVERFLOW,
  output Carry_Flag
);

  wire and_1_out, and_2_out, or_1_out, sumador_completo_2_bits_1_cout, sumador_completo_2_bits_1_s,
       sumador_completo_2_bits_2_cout, sumador_completo_2_bits_2_s, xor_1_out;

  and and_1 (and_1_out, F, I);
  xor xor_1 (xor_1_out, F, I);
  and and_2 (and_2_out, and_1_out, CS);
  and and_3 (S0, xor_1_out, CS);
  Sumador_Completo_2_bits sumador_completo_2_bits_1 (
    .e0(E), .e1(H), .Cin(and_2_out), .S(sumador_completo_2_bits_1_s), .Cout(sumador_completo_2_bits_1_cout));
  and and_4 (S1, CS, sumador_completo_2_bits_1_s);
  Sumador_Completo_2_bits sumador_completo_2_bits_2 (
    .e0(D), .e1(G), .Cin(sumador_completo_2_bits_1_cout), .S(sumador_completo_2_bits_2_s),
    .Cout(sumador_completo_2_bits_2_cout));
  and and_5 (OVERFLOW, CS, sumador_completo_2_bits_2_cout);
  or or_1 (or_1_out, sumador_completo_2_bits_2_cout, sumador_completo_2_bits_1_cout, and_2_out);
  and and_6 (S2, CS, sumador_completo_2_bits_2_s);
  and and_7 (Carry_Flag, or_1_out, CS);
endmodule

module Funcion (
  input  D,
  input  E,
  input  F,
  input  G,
  input  CS,
  output S
);

  wire and_1_out, and_2_out, not_1_out, not_2_out, not_3_out, or_1_out, or_2_out, xnor_1_out;

  not not_1 (not_1_out, G);
  or or_1 (or_1_out, D, not_1_out);
  not not_2 (not_2_out, E);
  not not_3 (not_3_out, F);
  xnor xnor_1 (xnor_1_out, D, G);
  and and_1 (and_1_out, F, E, or_1_out);
  and and_2 (and_2_out, not_2_out, not_3_out, xnor_1_out);
  or or_2 (or_2_out, and_1_out, and_2_out);
  and and_3 (S, or_2_out, CS);
endmodule

module Paridad (
  input  D,
  input  E,
  input  F,
  input  G,
  input  H,
  input  I,
  input  CS,
  output out_8
);

  wire xor_1_out;

  xor xor_1 (xor_1_out, D, E, F, G, H, I);
  and and_1 (out_8, xor_1_out, CS);
endmodule

module Inversor_C2 (
  input  D,
  input  E,
  input  F,
  input  CS,
  output S0,
  output S1,
  output S2,
  output Zero_F
);

  wire not_1_out, not_2_out, not_3_out, not_4_out, not_5_out, not_6_out;

  not not_1 (not_1_out, D);
  not not_2 (not_2_out, E);
  not not_3 (not_3_out, F);
  Sumador_ALU sumador_alu_1 (
    .D(not_1_out), .E(not_2_out), .F(not_3_out), .G(1'b0), .H(1'b0), .I(1'b1), .CS(CS), .S2(S0), .S1(S1),
    .S0(S2));  // open: OVERFLOW, Carry_Flag
  not not_4 (not_4_out, S0);
  and and_1 (Zero_F, not_4_out, not_5_out, not_6_out);
  not not_5 (not_5_out, S1);
  not not_6 (not_6_out, S2);
endmodule

module Resta (
  input  CS,
  input  D,
  input  E,
  input  F,
  input  G,
  output S0,
  output S1,
  output Overflow,
  output ZeroF
);

  wire and_1_out, and_2_out, and_3_out, and_4_out, and_5_out, and_6_out, and_7_out, and_8_out, and_9_out,
       and_10_out, and_11_out, and_12_out, not_1_out, not_2_out, not_3_out, not_4_out, not_5_out, not_6_out,
       not_7_out, not_8_out, not_9_out, not_10_out, not_11_out, not_12_out, not_13_out, not_14_out,
       not_15_out, not_16_out, not_17_out, not_18_out, not_19_out, not_20_out, or_1_out, or_2_out, or_3_out,
       or_4_out;

  not not_1 (not_1_out, F);
  not not_2 (not_2_out, G);
  not not_3 (not_3_out, F);
  not not_4 (not_4_out, F);
  not not_5 (not_5_out, G);
  not not_6 (not_6_out, E);
  not not_7 (not_7_out, F);
  not not_8 (not_8_out, G);
  not not_9 (not_9_out, D);
  not not_10 (not_10_out, E);
  not not_11 (not_11_out, D);
  not not_12 (not_12_out, E);
  not not_13 (not_13_out, D);
  not not_14 (not_14_out, E);
  not not_15 (not_15_out, F);
  not not_16 (not_16_out, G);
  not not_17 (not_17_out, D);
  not not_18 (not_18_out, F);
  not not_19 (not_19_out, E);
  not not_20 (not_20_out, G);
  and and_1 (and_1_out, D, not_1_out, not_2_out);
  and and_2 (and_2_out, D, E, not_3_out);
  and and_3 (and_3_out, E, not_4_out, not_5_out);
  and and_4 (and_4_out, D, not_6_out, not_7_out, G);
  and and_5 (and_5_out, D, E, not_8_out);
  and and_6 (and_6_out, not_9_out, not_10_out, G);
  and and_7 (and_7_out, not_11_out, F);
  and and_8 (and_8_out, not_12_out, F, G);
  and and_9 (and_9_out, not_13_out, not_14_out, not_15_out, not_16_out);
  and and_10 (and_10_out, not_17_out, E, not_18_out, G);
  and and_11 (and_11_out, D, not_19_out, F, not_20_out);
  and and_12 (and_12_out, D, E, F, G);
  or or_1 (or_1_out, and_1_out, and_2_out);
  or or_2 (or_2_out, and_3_out, and_4_out, and_5_out);
  or or_3 (or_3_out, and_6_out, and_7_out, and_8_out);
  or or_4 (or_4_out, and_9_out, and_10_out, and_11_out, and_12_out);
  and and_13 (S0, or_1_out, CS);
  and and_14 (S1, or_2_out, CS);
  and and_15 (Overflow, or_3_out, CS);
  and and_16 (ZeroF, or_4_out, CS);
endmodule
