// Logisim project semaforo.circ as structural Verilog: 1 circuit, main circuit main
module main (
);

  wire and_1_out, and_2_out, and_3_out, and_4_out, and_5_out, and_6_out, and_7_out, clock_1_out, d_ff_1_q,
       d_ff_1_qn, d_ff_2_q, d_ff_2_qn, d_ff_3_q, d_ff_3_qn, not_2_out, not_3_out, or_1_out, xor_1_out;

  Clock clock_1 (.out(clock_1_out));
  D_Flip_Flop d_ff_1 (.clk(clock_1_out), .D(or_1_out), .Q(d_ff_1_q), .Qn(d_ff_1_qn));  // open: preset, en, reset
  // NOT_Gate not_1 has open pins: in=d_ff_3_q, out=open
  not not_2 (not_2_out, d_ff_2_q);
  not not_3 (not_3_out, d_ff_1_q);
  and and_1 (and_1_out, d_ff_1_qn, d_ff_2_q, d_ff_3_q);
  and and_2 (and_2_out, d_ff_1_q, d_ff_3_qn);
  or or_1 (or_1_out, and_1_out, and_2_out, and_3_out);
  D_Flip_Flop d_ff_2 (.clk(clock_1_out), .D(xor_1_out), .Q(d_ff_2_q), .Qn(d_ff_2_qn));  // open: preset, en, reset
  and and_3 (and_3_out, d_ff_1_q, d_ff_2_qn);
  xor xor_1 (xor_1_out, d_ff_3_q, d_ff_2_q);
  and and_4 (and_4_out, d_ff_2_q, not_3_out);
  and and_5 (and_5_out, not_2_out, not_3_out);
  and and_6 (and_6_out, d_ff_1_q, d_ff_2_q);
  and and_7 (and_7_out, d_ff_1_q, not_2_out);
  D_Flip_Flop d_ff_3 (.clk(clock_1_out), .D(d_ff_3_qn), .Q(d_ff_3_q), .Qn(d_ff_3_qn));  // open: preset, en, reset
  LED led_1 (.in(d_ff_1_q));
  LED led_2 (.in(and_4_out));
  LED led_3 (.in(and_5_out));
  LED led_4 (.in(not_3_out));
  LED led_5 (.in(and_6_out));
  LED led_6 (.in(and_7_out));
  LED led_7 (.in(not_3_out));
  LED led_8 (.in(and_6_out));
  LED led_9 (.in(and_7_out));
  LED led_10 (.in(d_ff_1_q));
  LED led_11 (.in(and_4_out));
  LED led_12 (.in(and_5_out));

  // Notes on the sheet:
  //   a
  //   c
  //   b
  //   a
  //   (No utilizada)
  //   b
  //   c
endmodule
