// Logisim project prueba1.circ as structural Verilog: 1 circuit, main circuit main
module main (
);

  wire transistor_1_out, undriven;

  LED led_1 ();  // open: in
  LED led_2 (.in(transistor_1_out));
  LED led_3 (.in(undriven));
  LED led_4 (.in(transistor_1_out));
  Transistor transistor_1 (.in(undriven), .out(transistor_1_out));  // open: gate
endmodule
